# Fritzing sketch mini_araba (saved by Fritzing 0.9.5d)
breadboards: 1

parts:
  Parça1 = Arduino Uno (Rev3)  # not connected
  M1 = Dagu DGServo 9g (End View) [part_number=RS001B]
  J1 = Piezo Speaker
  BT1 = Bluetooth HC-06u [package=THT]
  L298N1 = L298N DC motor driver
  Raspberry_Pi_1 = Raspberry Pi 4 [part_number=RPI-4-b]
  M2 = DC Motor  # not connected
  BAT1 = BC9VPC [package=bc9vpc]
  Parça2 = Adafruit Proto Shield for Arduino Kit - v.5
  R1 = Resistor [tolerance=±5% resistance=220 package=THT]
  R2 = Resistor [tolerance=±5% resistance=220 package=THT]
  R3 = Resistor [tolerance=±5% resistance=220 package=THT]
  M3 = bb-usb-cable [package=THT]  # not connected
  U1 = TRANSCHIPTC5747 [package=camera_sfv24r-2st_2]  # not connected
  BAT2 = BC9VPC [package=bc9vpc]

nets:
  GND: M1.gnd, J1.pin2, Parça2.GND, Parça2.P$2, Parça2.P$4, R1.Pin_1, R2.Pin_0
  VCC: M1.vcc, Raspberry_Pi_1.5V
  N1: M1.pulse, Parça2.D8
  N2: J1.pin1, Parça2.D5
  N3: BT1.VCC, R2.Pin_1, R3.Pin_0
  N4: BT1.GND, Parça2.D7
  N5: BT1.RXD, Parça2.+5V, Parça2.P$1
  N6: L298N1.IN3, Parça2.D3
  N7: L298N1.IN4, Parça2.D4
  N8: BAT1.V+, BAT2.V+
  N9: BAT1.V-, BAT2.V-
  N10: Parça2.D6, R3.Pin_1

custom parts:
  Bluetooth HC-06u: Bluetooth HC-06 - face up, pins down 16.5mm x 37.5mm PCB
  L298N DC motor driver: 2x DC motor driver with 78M05 positive voltage regulator (7..35 V) L298N: max 46 V, 2 A Set 5 V Enable jumper to enable 5 V regultor (needed for the L298N) and +5 V output at screw terminal or supply external +5 V at screw terminal Set ENA and/or ENB to +5 V to enable motor permanently or supply ENA and/or ENB with PWM signal IN1 and IN2 set rotation directory for motor A (OUT1/OUT2) IN2 and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
  Raspberry Pi 4: The RPi4, a faster version of the awesome Raspberry Pi 2 B ARM Board with 40 pin gpio. Ready for special Raspberry Pi B+ and RPi2 Hat (Hardware attached (on) top)
  Adafruit Proto Shield for Arduino Kit - v.5: Arduino prototyping shield designed by Adafruit Industries
  bb-usb-cable: Breadboard only, no connectors USB cable for the Raspberry PIs.
